# Fritzing sketch CyGate4-Keypad (saved by Fritzing 0.9.3b)
circuit board: 8.46667cm x 5.64444cm
breadboards: 1

parts:
  J1 = screw terminal, 4 pins
  Arduino_Micro_Rev3 = Arduino Micro (Rev3)
  R1 = Resistor [tolerance=±5% resistance=4.7k package=THT]
  R2 = Resistor [tolerance=±5% resistance=4.7k package=THT]
  J2 = male pin header, 8 pins [form="♂ (male)"]
  J3 = male pin header, 5 pins [form="♂ (male)"]
  C1 = Ceramic Capacitor [capacitance=0.1mF package="100 mil [THT, multilayer]"]

nets:
  N1: J1.pin1, Arduino_Micro_Rev3.GND, J3.pin1, C1.0
  N2: J1.pin2, Arduino_Micro_Rev3.5V, R1.Pin_1, R2.Pin_1, J3.pin2, J3.pin3, C1.1
  N3: J1.pin3, Arduino_Micro_Rev3.D3/SCL, R2.Pin_0
  N4: J1.pin4, Arduino_Micro_Rev3.D2/SDA, R1.Pin_0
  N5: Arduino_Micro_Rev3.D4_PWM/A6, J2.pin8
  N6: Arduino_Micro_Rev3.D5_PWM, J2.pin7
  N7: Arduino_Micro_Rev3.D6_PWM/A7, J2.pin6
  N8: Arduino_Micro_Rev3.D7, J2.pin5
  N9: Arduino_Micro_Rev3.D8_PWM/A8, J2.pin4
  N10: Arduino_Micro_Rev3.D9_PWM/A9, J2.pin3
  N11: Arduino_Micro_Rev3.D10_PWM/A10, J2.pin2
  N12: Arduino_Micro_Rev3.D11_PWM, J2.pin1
  N13: Arduino_Micro_Rev3.D12_PWM/A11, J3.pin5
  N14: Arduino_Micro_Rev3.D13_PWM, J3.pin4

notes:
  KEYPAD
  1
  Gnd
  FAB 001001 ASSY 001001
  +5VDC
  SDA
  SCL
  TX
  RX
  LCD
  CyGate4 - Keypad Rev 1.0
  Copyright (c) 2021 Cyrus Brunner
  www.cyrusbuilt.net
  CyGate4 - Keypad, Keypad entry and display module for CyGate4, 1.0
  GND
  To LCD
  To Keypad
